# Fritzing sketch Nano_ESP32-PCB_V03+NanoESP32 (saved by Fritzing 1.0.3b)
circuit board: 9cm x 6cm

parts:
  R5 = Resistor [tolerance=±5% resistance=470 power=0.25 package=THT]
  1000_uF = Electrolytic Capacitor [capacitance=1mF voltage=16V package="100 mil [THT, electrolytic]"]
  RTCclock2 = female pin header, 6 pins [form="♀ (female)"]
  LDR = male pin header, 2 pins [form="♂ (male)"]
  R13 = Resistor [tolerance=±5% resistance=10k power=0.25W package=THT]
  RTC-clock = female pin header, 6 pins [form="♀ (female)"]
  RTCclock6 = female pin header, 3 pins [form="♀ (female)"]
  RTCclock4 = female pin header, 3 pins [form="♀ (female)"]
  RTCclock3 = female pin header, 3 pins [form="♀ (female)"]
  RTCclock9 = female pin header, 6 pins [form="♀ (female)"]
  DCF = female pin header, 3 pins [form="♀ (female)"]
  R18 = Resistor [tolerance=±5% resistance=470 power=0.25W package=THT]
  RTCclock11 = female pin header, 4 pins [form="♀ (female)"]
  R19 = Resistor [tolerance=±5% resistance=470 power=0.25W package=THT]
  - = LED - 3mm [color="Red (633nm)" current=0.030A package="3 mm [THT]"]
  -_2 = LED - 3mm [color="Yellow (592nm)" current=0.030A package="3 mm [THT]"]
  Rotary = female pin header, 5 pins [form="♀ (female)"]
  J1 = screw terminal, 2 pins
  1N5817 = Rectifier Diode [part_number=1N4001 package="300 mil [THT]"]
  5V_Out_GND = female pin header, 3 pins [form="♀ (female)"]
  AMS1117_3v3 = female pin header, 3 pins [form="♀ (female)"]
  R20 = Resistor [tolerance=±5% resistance=470 power=0.25 part_number=...Ω package=THT]  # not connected
  RTCclock12 = female pin header, 3 pins [form="♀ (female)"]
  RTCclock13 = female pin header, 3 pins [form="♀ (female)"]
  RTCclock14 = female pin header, 2 pins [form="♀ (female)"]
  74AHCT125 = 74HC08 Logic AND Gate [part_number=74HC08 package="DIP (Dual Inline) [THT]"]
  RTCclock15 = female pin header, 2 pins [form="♀ (female)"]
  J2 = screw terminal, 2 pins
  1N5817_2 = Rectifier Diode [part_number=1N4001 package="300 mil [THT]"]
  TX-RX = male pin header, 3 pins [form="♂ (male)"]
  C1 = Electrolytic Capacitor [capacitance=10µF package="100 mil [THT, electrolytic]"]
  R24 = Resistor [tolerance=±5% resistance=10k power=0.25W package=THT]
  R25 = Resistor [tolerance=±5% resistance=10k power=0.25W package=THT]
  J5 = female pin header, 15 pins [form="♀ (female)"]  # not connected
  J7 = female pin header, 15 pins [form="♀ (female)"]  # not connected
  A1 = Arduino Nano ESP32  # not connected

nets:
  N1: R5.Pin_0, RTCclock6.pin2
  N2: R5.Pin_1, 74AHCT125.1Y
  N3: 1000_uF.-, R13.Pin_0, RTC-clock.pin1, RTCclock6.pin1, RTCclock3.pin1, RTCclock3.pin2, RTCclock3.pin3, DCF.pin3, -.cathode, -_2.cathode, Rotary.pin5, J1.pin1, 5V_Out_GND.pin1, AMS1117_3v3.pin1, RTCclock13.pin1, RTCclock13.pin2, RTCclock13.pin3, RTCclock14.pin2, 74AHCT125.1A, 74AHCT125.2A, 74AHCT125.GND, 74AHCT125.4B, RTCclock15.pin1, J2.pin1, TX-RX.pin1, C1.-
  N4: 1000_uF.+, RTCclock6.pin3, J1.pin2, 1N5817.anode, 5V_Out_GND.pin3, AMS1117_3v3.pin3, 74AHCT125.VCC
  N5: RTCclock2.pin1, RTCclock9.pin1
  N6: RTCclock2.pin2, RTCclock9.pin2
  N7: RTCclock2.pin3, RTCclock9.pin3
  N8: RTCclock2.pin4, RTCclock9.pin4
  N9: RTCclock2.pin5, RTCclock9.pin5
  N10: RTCclock2.pin6, RTCclock9.pin6
  N11: LDR.pin1, R13.Pin_1
  N12: LDR.pin2, RTC-clock.pin2, DCF.pin1, Rotary.pin4, 5V_Out_GND.pin2, AMS1117_3v3.pin2, RTCclock12.pin1, RTCclock12.pin2, RTCclock12.pin3
  N13: RTC-clock.pin3, R25.Pin_0
  N14: RTC-clock.pin4, R24.Pin_0
  N15: RTCclock4.pin1, RTCclock4.pin2, RTCclock4.pin3, 1N5817.cathode
  N16: R18.Pin_0, -.anode
  N17: R18.Pin_1, RTCclock11.pin2
  N18: RTCclock11.pin1, R19.Pin_1, -_2.anode
  N19: Rotary.pin2, RTCclock14.pin1
  N20: 74AHCT125.2Y, RTCclock15.pin2
  N21: J2.pin2, 1N5817_2.anode, C1.+

notes:
  +
  -
  Gnd
  5V
  32K
  SQW
  SCL
  SDA
  3V3
  Power
  A5
  A4
  D5
  DCF signal
  D8
  D3
  D4
  A3
  A2
  TX
  RX
  DT
  SW
  CLK
  D9
  D10
  D11
  D12
  D6
  D7
  A1
  A6
  A7
  Vin
  Rst
  D2
  A0
  Aref
  D13
  Signal to LED-strip
  USB
  Connect to use
  D6 at 5V
  D7 at 5V
  6-21V
  5V-USB
  To
  resistors SDA SCL
  Optional pull up or down

custom parts:
  Arduino Nano ESP32: Arduino® Nano ESP32 tht.
